// Logisim project Counter_Base.circ as structural Verilog: 1 circuit, main circuit main
module main (
  input  Power
);

  wire _2_0__prime_q, _2_0__prime_qn, _2_1__prime_q, _2_1__prime_qn, _2_2__prime_q, _2_2__prime_qn,
       _2_3__prime_qn, and_1_out, and_2_out, and_3_out, and_4_out, and_5_out, and_6_out, and_7_out,
       and_8_out, and_9_out, and_10_out, and_11_out, and_12_out, and_13_out, and_14_out, and_15_out,
       and_16_out, and_17_out, and_18_out, and_19_out, and_20_out, and_21_out, and_22_out, and_23_out,
       and_24_out, and_25_out, and_26_out, and_27_out, and_28_out, and_29_out, and_30_out, and_31_out,
       and_32_out, and_33_out, and_34_out, and_35_out, and_36_out, and_37_out, and_38_out, and_39_out,
       and_40_out, and_41_out, and_42_out, and_43_out, and_44_out, and_45_out, and_46_out, and_47_out,
       and_48_out, Clock_out, not_1_out, not_2_out, not_3_out, not_4_out, or_1_out, or_2_out, or_3_out,
       or_4_out, or_5_out, or_6_out, or_7_out, or_8_out, or_9_out, or_10_out, or_11_out, or_12_out,
       or_13_out, or_14_out, or_15_out, or_16_out, or_17_out, or_18_out, or_19_out, or_20_out, or_21_out,
       or_22_out, or_23_out, or_24_out, or_25_out, or_26_out, or_27_out, Reset_out;

  Clock Clock (.out(Clock_out));
  Button Reset (.out(Reset_out));
  J_K_Flip_Flop _2_0__prime (
    .J(Power), .clk(Clock_out), .K(Power), .Q(_2_0__prime_q), .Qn(_2_0__prime_qn), .reset(Reset_out));  // open: preset, en
  J_K_Flip_Flop _2_1__prime (
    .J(Power), .clk(_2_0__prime_q), .K(Power), .Q(_2_1__prime_q), .Qn(_2_1__prime_qn), .reset(Reset_out));  // open: preset, en
  J_K_Flip_Flop _2_2__prime (
    .J(Power), .clk(_2_1__prime_q), .K(Power), .Q(_2_2__prime_q), .Qn(_2_2__prime_qn), .reset(Reset_out));  // open: preset, en
  J_K_Flip_Flop _2_3__prime (
    .J(Power), .clk(_2_2__prime_q), .K(Power), .Qn(_2_3__prime_qn), .reset(Reset_out));  // open: Q, preset, en
  or or_1 (or_1_out, and_1_out, and_2_out);
  or or_2 (or_2_out, and_3_out, and_4_out);
  or or_3 (or_3_out, or_1_out, or_2_out);
  or or_4 (or_4_out, and_5_out, and_6_out);
  or or_5 (or_5_out, and_7_out, _2_0__prime_qn);
  or or_6 (or_6_out, or_4_out, or_5_out);
  LED led_1 (.in(_2_3__prime_qn));
  and and_1 (and_1_out, not_1_out, not_3_out);
  and and_2 (and_2_out, _2_3__prime_qn, not_4_out);
  and and_3 (and_3_out, _2_2__prime_qn, _2_0__prime_qn);
  and and_4 (and_4_out, not_2_out, _2_1__prime_qn);
  and and_5 (and_5_out, not_4_out, not_2_out);
  and and_6 (and_6_out, _2_2__prime_qn, _2_1__prime_qn);
  and and_7 (and_7_out, not_1_out, _2_3__prime_qn);
  LED led_2 (.in(_2_2__prime_qn));
  LED led_3 (.in(_2_1__prime_qn));
  not not_1 (not_1_out, _2_2__prime_qn);
  not not_2 (not_2_out, _2_3__prime_qn);
  LED led_4 (.in(_2_0__prime_qn));
  not not_3 (not_3_out, _2_0__prime_qn);
  not not_4 (not_4_out, _2_1__prime_qn);
  and and_8 (and_8_out, not_3_out, _2_2__prime_qn);
  and and_9 (and_9_out, _2_3__prime_qn, _2_2__prime_qn);
  and and_10 (and_10_out, _2_2__prime_qn, not_4_out);
  and and_11 (and_11_out, not_4_out, _2_3__prime_qn);
  and and_12 (and_12_out, not_3_out, not_4_out);
  and and_13 (and_13_out, not_4_out, _2_2__prime_qn);
  and and_14 (and_14_out, not_4_out, not_1_out);
  and and_15 (and_15_out, _2_1__prime_qn, _2_2__prime_qn);
  and and_16 (and_16_out, not_3_out, _2_1__prime_qn);
  and and_17 (and_17_out, not_3_out, _2_1__prime_qn);
  and and_18 (and_18_out, _2_3__prime_qn, not_1_out);
  and and_19 (and_19_out, and_18_out, not_4_out);
  or or_7 (or_7_out, and_8_out, and_9_out);
  or or_8 (or_8_out, or_7_out, or_9_out);
  or or_9 (or_9_out, and_10_out, and_11_out);
  and and_20 (and_20_out, _2_1__prime_qn, not_1_out);
  and and_21 (and_21_out, and_20_out, not_2_out);
  and and_22 (and_22_out, and_12_out, not_2_out);
  or or_10 (or_10_out, and_22_out, and_23_out);
  and and_23 (and_23_out, and_13_out, not_2_out);
  and and_24 (and_24_out, and_14_out, _2_3__prime_qn);
  or or_11 (or_11_out, and_24_out, and_25_out);
  and and_25 (and_25_out, and_15_out, _2_3__prime_qn);
  and and_26 (and_26_out, and_16_out, _2_2__prime_qn);
  or or_12 (or_12_out, and_26_out, and_27_out);
  and and_27 (and_27_out, and_17_out, _2_3__prime_qn);
  or or_13 (or_13_out, not_2_out, and_19_out);
  or or_14 (or_14_out, or_8_out, and_21_out);
  or or_15 (or_15_out, or_10_out, or_16_out);
  or or_16 (or_16_out, or_11_out, or_12_out);
  _7_Segment_Display u_7_segment_display_1 (
    .f(or_13_out), .a(or_13_out), .b(Power), .e(or_13_out), .d(or_13_out), .c(Power));  // open: g, dp
  _7_Segment_Display u_7_segment_display_2 (
    .g(or_14_out), .f(or_15_out), .a(or_3_out), .b(or_20_out), .e(or_22_out), .d(or_27_out), .c(or_6_out));  // open: dp
  and and_28 (and_28_out, not_4_out, not_3_out);
  or or_17 (or_17_out, and_28_out, and_29_out);
  and and_29 (and_29_out, not_4_out, _2_3__prime_qn);
  and and_30 (and_30_out, not_3_out, _2_3__prime_qn);
  and and_31 (and_31_out, _2_0__prime_qn, _2_1__prime_qn);
  and and_32 (and_32_out, and_31_out, not_2_out);
  and and_33 (and_33_out, not_1_out, not_3_out);
  and and_34 (and_34_out, _2_3__prime_qn, not_4_out);
  and and_35 (and_35_out, and_34_out, not_3_out);
  and and_36 (and_36_out, not_3_out, _2_1__prime_qn);
  and and_37 (and_37_out, and_36_out, not_2_out);
  and and_38 (and_38_out, not_1_out, not_3_out);
  and and_39 (and_39_out, not_4_out, _2_3__prime_qn);
  and and_40 (and_40_out, and_39_out, _2_2__prime_qn);
  and and_41 (and_41_out, _2_2__prime_qn, not_4_out);
  and and_42 (and_42_out, and_41_out, _2_0__prime_qn);
  and and_43 (and_43_out, _2_0__prime_qn, _2_2__prime_qn);
  and and_44 (and_44_out, and_43_out, _2_3__prime_qn);
  and and_45 (and_45_out, not_2_out, not_1_out);
  and and_46 (and_46_out, and_45_out, _2_1__prime_qn);
  and and_47 (and_47_out, _2_1__prime_qn, not_2_out);
  and and_48 (and_48_out, and_47_out, not_3_out);
  or or_18 (or_18_out, and_30_out, and_32_out);
  or or_19 (or_19_out, or_18_out, or_17_out);
  or or_20 (or_20_out, not_1_out, or_19_out);
  or or_21 (or_21_out, and_33_out, and_35_out);
  or or_22 (or_22_out, and_37_out, or_21_out);
  or or_23 (or_23_out, and_38_out, and_40_out);
  or or_24 (or_24_out, and_42_out, and_44_out);
  or or_25 (or_25_out, or_24_out, or_23_out);
  or or_26 (or_26_out, and_46_out, and_48_out);
  or or_27 (or_27_out, or_26_out, or_25_out);

  // Notes on the sheet:
  //   W
  //   Y
  //   X
  //   Z
endmodule
